# Fritzing sketch Arduino328_ICSP_Connection (saved by Fritzing 0.9.10b)
breadboards: 1

parts:
  元件1 = Arduino Uno (Rev3)
  U1 = atmega328 [package=dip]
  LED1 = LED - 3mm [color="Red (633nm)" current=0.030 package="3 mm [THT]"]
  R1 = Resistor [tolerance=±5% resistance=220 package="0402 [SMD]"]
  XTAL1 = Crystal [frequency="16 Mhz" package=SMD]
  C1 = Tantalum Capacitor [capacitance=1μF voltage=35V package="100 mil [THT, tantalum]"]
  C2 = Tantalum Capacitor [capacitance=1μF voltage=35V package="100 mil [THT, tantalum]"]

nets:
  N1: 元件1.D10_PWM/SS, U1.RESET
  N2: 元件1.D11_PWM/MOSI, U1.D11_(PWM)
  N3: 元件1.D12/MISO, U1.D12
  N4: 元件1.D13/SCK, U1.D13, LED1.anode
  5V: 元件1.5V, U1.VCC
  N5: 元件1.GND, U1.GND#7, R1.Pin_0, C1.-, C2.-
  N6: U1.XLAT1, XTAL1.pin_0, C2.+
  N7: U1.XLAT2, XTAL1.pin_1, C1.+
  N8: LED1.cathode, R1.Pin_1
