# Fritzing sketch icsp_connection (saved by Fritzing 0.9.10b)

parts:
  元件1 = Arduino Uno (Rev3)
  元件2 = Arduino Uno (Rev3)

nets:
  N1: 元件1.D10_PWM/SS, 元件2.RESET
  N2: 元件1.D11_PWM/MOSI, 元件2.D11_PWM/MOSI
  N3: 元件1.D12/MISO, 元件2.D12/MISO
  N4: 元件1.D13/SCK, 元件2.D13/SCK
  5V: 元件1.5V, 元件2.5V
  GND: 元件1.GND, 元件2.GND
